// Logisim project D.circ as structural Verilog: 1 circuit, main circuit main
module main (
  output A,
  output B,
  output C,
  output D,
  output E,
  output F,
  output G
);

  wire and_1_out, and_2_out, and_3_out, and_4_out, and_5_out, and_6_out, and_7_out, and_8_out, and_9_out,
       and_10_out, and_11_out, and_12_out, and_13_out, and_14_out, and_15_out, and_16_out, and_17_out,
       and_18_out, and_19_out, and_20_out, and_21_out, and_22_out, clock_1_out, FF0_q, FF0_qn, FF1_q, FF1_qn,
       FF2_q, FF2_qn, FF3_q, FF3_qn, not_1_out, not_2_out, not_3_out, not_4_out, or_1_out, or_2_out,
       or_10_out, xor_1_out;

  Clock clock_1 (.out(clock_1_out));
  D_Flip_Flop FF3 (.D(or_10_out), .clk(clock_1_out), .Q(FF3_q), .Qn(FF3_qn));  // open: preset, reset
  D_Flip_Flop FF2 (.D(or_2_out), .clk(clock_1_out), .Q(FF2_q), .Qn(FF2_qn));  // open: preset, reset
  D_Flip_Flop FF1 (.D(xor_1_out), .clk(clock_1_out), .Q(FF1_q), .Qn(FF1_qn));  // open: preset, reset
  D_Flip_Flop FF0 (.D(FF0_qn), .clk(clock_1_out), .Q(FF0_q), .Qn(FF0_qn));  // open: preset, reset
  not not_1 (not_1_out, FF3_q);
  not not_2 (not_2_out, FF2_q);
  not not_3 (not_3_out, FF1_q);
  not not_4 (not_4_out, FF0_q);
  and and_1 (and_1_out, FF0_q, FF1_q, FF2_q);
  or or_1 (or_1_out, FF0_qn, FF1_qn);
  and and_2 (and_2_out, or_1_out, FF2_q);
  and and_3 (and_3_out, FF0_q, FF1_q, FF2_qn, FF3_qn);
  and and_4 (and_4_out, not_1_out, not_3_out);
  and and_5 (and_5_out, FF2_q, not_4_out);
  and and_6 (and_6_out, FF3_q, not_4_out);
  and and_7 (and_7_out, FF1_q, FF0_q);
  and and_8 (and_8_out, not_3_out, not_4_out);
  and and_9 (and_9_out, FF3_q, FF1_q);
  and and_10 (and_10_out, FF3_q, not_4_out);
  and and_11 (and_11_out, not_1_out, FF0_q);
  and and_12 (and_12_out, FF2_q, not_3_out);
  and and_13 (and_13_out, FF2_q, not_4_out);
  and and_14 (and_14_out, FF2_q, not_4_out);
  and and_15 (and_15_out, not_3_out, not_4_out);
  and and_16 (and_16_out, FF2_q, not_3_out, not_4_out);
  and and_17 (and_17_out, not_2_out, not_3_out, FF0_q);
  and and_18 (and_18_out, FF3_q, FF1_q);
  and and_19 (and_19_out, not_2_out, not_4_out);
  and and_20 (and_20_out, FF1_q, not_4_out);
  and and_21 (and_21_out, not_1_out, not_3_out, FF0_q);
  or or_2 (or_2_out, and_2_out, and_3_out);
  xor xor_1 (xor_1_out, FF1_q, FF0_q);
  or or_3 (A, and_4_out, and_5_out);
  or or_4 (B, FF2_q, and_6_out, and_7_out, and_8_out);
  or or_5 (C, and_9_out, and_10_out, and_11_out, and_12_out);
  or or_6 (D, FF3_q, not_3_out, and_13_out);
  or or_7 (E, FF3_q, and_14_out, and_15_out);
  or or_8 (F, and_16_out, and_17_out);
  or or_9 (G, and_18_out, and_19_out, and_20_out, and_21_out);
  or or_10 (or_10_out, and_1_out, and_22_out);
  and and_22 (and_22_out, FF3_q, or_1_out);
  _7_Segment_Display u_7_segment_display_1 (.g(G), .f(F), .a(A), .b(B), .e(E), .d(D), .c(C));  // open: dp
endmodule
