// Logisim project MPOS.circ as structural Verilog: 1 circuit, main circuit main
module main (
  input  w,
  input  x,
  input  y,
  input  z,
  output A,
  output B,
  output C,
  output D,
  output E,
  output F,
  output G
);

  wire not_1_out, not_2_out, not_3_out, not_4_out, or_1_out, or_2_out, or_3_out, or_4_out, or_5_out,
       or_6_out, or_7_out, or_8_out, or_9_out, or_10_out, or_11_out, or_12_out, or_13_out, or_14_out,
       or_15_out, or_16_out;

  not not_1 (not_1_out, w);
  not not_2 (not_2_out, x);
  not not_3 (not_3_out, y);
  not not_4 (not_4_out, z);
  and and_1 (A, not_1_out, or_1_out, or_2_out);
  or or_1 (or_1_out, x, not_3_out);
  or or_2 (or_2_out, not_3_out, not_4_out);
  or or_3 (or_3_out, x, y, not_4_out);
  and and_2 (B, or_3_out, or_4_out);
  or or_4 (or_4_out, w, x, not_3_out, z);
  or or_5 (or_5_out, w, x, z);
  and and_3 (C, or_5_out, or_6_out, or_7_out);
  or or_6 (or_6_out, w, not_3_out, z);
  or or_7 (or_7_out, not_1_out, y, not_4_out);
  or or_8 (or_8_out, w, x, not_3_out);
  and and_4 (D, or_8_out, or_9_out);
  or or_9 (or_9_out, w, not_3_out, not_4_out);
  or or_10 (or_10_out, w, not_4_out);
  and and_5 (E, or_10_out, or_11_out);
  or or_11 (or_11_out, w, x, not_3_out);
  or or_12 (or_12_out, x, z);
  and and_6 (F, not_3_out, or_12_out, or_13_out);
  or or_13 (or_13_out, not_2_out, not_4_out);
  or or_14 (or_14_out, w, not_3_out, not_4_out);
  or or_15 (or_15_out, not_1_out, y, not_4_out);
  and and_7 (G, or_14_out, or_15_out, or_16_out);
  or or_16 (or_16_out, not_2_out, y, z);
  _7_Segment_Display u_7_segment_display_1 (.g(G), .f(F), .a(A), .b(B), .e(E), .d(D), .c(C));  // open: dp
endmodule
