// Logisim project MSOP.circ as structural Verilog: 1 circuit, main circuit main
module main (
  input  w,
  input  x,
  input  y,
  input  z,
  output A,
  output B,
  output C,
  output D,
  output E,
  output F,
  output G
);

  wire and_1_out, and_2_out, and_3_out, and_4_out, and_5_out, and_6_out, and_7_out, and_8_out, and_9_out,
       and_10_out, and_11_out, and_12_out, and_13_out, and_14_out, and_15_out, and_16_out, and_17_out,
       and_18_out, not_1_out, not_2_out, not_3_out, not_4_out;

  not not_1 (not_1_out, w);
  not not_2 (not_2_out, y);
  not not_3 (not_3_out, x);
  not not_4 (not_4_out, z);
  and and_1 (and_1_out, not_1_out, not_2_out);
  or or_1 (A, and_1_out, and_2_out);
  and and_2 (and_2_out, x, not_4_out);
  and and_3 (and_3_out, w, not_4_out);
  and and_4 (and_4_out, y, z);
  and and_5 (and_5_out, not_2_out, not_4_out);
  and and_6 (and_6_out, w, y);
  and and_7 (and_7_out, w, not_4_out);
  and and_8 (and_8_out, not_1_out, z);
  and and_9 (and_9_out, x, not_2_out);
  or or_2 (D, w, not_2_out, and_10_out);
  and and_10 (and_10_out, x, not_4_out);
  and and_11 (and_11_out, x, not_4_out);
  or or_3 (E, w, and_11_out, and_12_out);
  and and_12 (and_12_out, not_2_out, not_4_out);
  and and_13 (and_13_out, x, not_2_out, not_4_out);
  or or_4 (F, and_13_out, and_14_out);
  and and_14 (and_14_out, not_3_out, not_2_out, z);
  and and_15 (and_15_out, w, y);
  and and_16 (and_16_out, not_3_out, not_4_out);
  and and_17 (and_17_out, y, not_4_out);
  and and_18 (and_18_out, not_1_out, not_2_out, z);
  or or_5 (B, x, and_3_out, and_4_out, and_5_out);
  or or_6 (C, and_6_out, and_7_out, and_8_out, and_9_out);
  or or_7 (G, and_15_out, and_16_out, and_17_out, and_18_out);
  _7_Segment_Display u_7_segment_display_1 (.g(G), .f(F), .a(A), .b(B), .e(E), .d(D), .c(C));  // open: dp
endmodule
