// Logisim project NAND.circ as structural Verilog: 1 circuit, main circuit main
module main (
  input  w,
  input  x,
  input  y,
  input  z,
  output A,
  output B,
  output C,
  output D,
  output E,
  output F,
  output G
);

  wire nand_1_out, nand_2_out, nand_3_out, nand_4_out, nand_5_out, nand_6_out, nand_7_out, nand_8_out,
       nand_9_out, nand_10_out, nand_11_out, nand_12_out, nand_13_out, nand_14_out, nand_15_out, nand_16_out,
       nand_17_out, nand_18_out, nand_19_out, nand_20_out, nand_21_out, nand_22_out;

  nand nand_1 (nand_1_out, w, w);
  nand nand_2 (nand_2_out, x, x);
  nand nand_3 (nand_3_out, y, y);
  nand nand_4 (nand_4_out, z, z);
  nand nand_5 (nand_5_out, nand_1_out, nand_3_out);
  nand nand_6 (nand_6_out, x, nand_4_out);
  nand nand_7 (nand_7_out, w, nand_4_out);
  nand nand_8 (nand_8_out, y, z);
  nand nand_9 (nand_9_out, nand_3_out, nand_4_out);
  nand nand_10 (nand_10_out, w, y);
  nand nand_11 (nand_11_out, w, nand_4_out);
  nand nand_12 (nand_12_out, nand_1_out, z);
  nand nand_13 (nand_13_out, x, nand_3_out);
  nand nand_14 (nand_14_out, x, nand_4_out);
  nand nand_15 (nand_15_out, x, nand_4_out);
  nand nand_16 (nand_16_out, nand_3_out, nand_4_out);
  nand nand_17 (nand_17_out, x, nand_3_out, nand_4_out);
  nand nand_18 (nand_18_out, nand_2_out, nand_3_out, z);
  nand nand_19 (nand_19_out, w, y);
  nand nand_20 (nand_20_out, nand_2_out, nand_4_out);
  nand nand_21 (nand_21_out, y, nand_4_out);
  nand nand_22 (nand_22_out, nand_1_out, nand_3_out, z);
  nand nand_23 (A, nand_5_out, nand_6_out);
  nand nand_24 (D, nand_1_out, y, nand_14_out);
  nand nand_25 (E, nand_1_out, nand_15_out, nand_16_out);
  nand nand_26 (F, nand_17_out, nand_18_out);
  nand nand_27 (B, nand_2_out, nand_7_out, nand_8_out, nand_9_out);
  nand nand_28 (C, nand_10_out, nand_11_out, nand_12_out, nand_13_out);
  nand nand_29 (G, nand_19_out, nand_20_out, nand_21_out, nand_22_out);
  _7_Segment_Display u_7_segment_display_1 (.g(G), .f(F), .a(A), .b(B), .e(E), .d(D), .c(C));  // open: dp
endmodule
