// Logisim project NOR.circ as structural Verilog: 1 circuit, main circuit main
module main (
  input  w,
  input  x,
  input  y,
  input  z,
  output A,
  output B,
  output C,
  output D,
  output E,
  output F,
  output G
);

  wire nor_1_out, nor_2_out, nor_3_out, nor_4_out, nor_5_out, nor_6_out, nor_7_out, nor_8_out, nor_9_out,
       nor_10_out, nor_11_out, nor_12_out, nor_13_out, nor_14_out, nor_15_out, nor_16_out, nor_17_out,
       nor_18_out, nor_19_out, nor_20_out;

  nor nor_1 (nor_1_out, w, w);
  nor nor_2 (nor_2_out, x, x);
  nor nor_3 (nor_3_out, y, y);
  nor nor_4 (nor_4_out, z, z);
  nor nor_5 (nor_5_out, x, nor_3_out);
  nor nor_6 (nor_6_out, nor_3_out, nor_4_out);
  nor nor_7 (nor_7_out, x, y, nor_4_out);
  nor nor_8 (nor_8_out, w, x, nor_3_out, z);
  nor nor_9 (nor_9_out, w, x, z);
  nor nor_10 (nor_10_out, w, nor_3_out, z);
  nor nor_11 (nor_11_out, nor_1_out, y, nor_4_out);
  nor nor_12 (nor_12_out, w, x, nor_3_out);
  nor nor_13 (nor_13_out, w, nor_3_out, nor_4_out);
  nor nor_14 (nor_14_out, w, nor_4_out);
  nor nor_15 (nor_15_out, w, x, nor_3_out);
  nor nor_16 (nor_16_out, x, z);
  nor nor_17 (nor_17_out, nor_2_out, nor_4_out);
  nor nor_18 (nor_18_out, w, nor_3_out, nor_4_out);
  nor nor_19 (nor_19_out, nor_1_out, y, nor_4_out);
  nor nor_20 (nor_20_out, nor_2_out, y, z);
  nor nor_21 (A, w, nor_5_out, nor_6_out);
  nor nor_22 (B, nor_7_out, nor_8_out);
  nor nor_23 (C, nor_9_out, nor_10_out, nor_11_out);
  nor nor_24 (D, nor_12_out, nor_13_out);
  nor nor_25 (E, nor_14_out, nor_15_out);
  nor nor_26 (F, y, nor_16_out, nor_17_out);
  nor nor_27 (G, nor_18_out, nor_19_out, nor_20_out);
  _7_Segment_Display u_7_segment_display_1 (.g(G), .f(F), .a(A), .b(B), .e(E), .d(D), .c(C));  // open: dp
endmodule
