// Logisim project SPOS.circ as structural Verilog: 1 circuit, main circuit main
module main (
  input  w,
  input  x,
  input  y,
  input  z,
  output a,
  output b,
  output c,
  output d,
  output e,
  output f,
  output g
);

  wire not_1_out, not_2_out, not_3_out, not_4_out, or_1_out, or_2_out, or_3_out, or_4_out, or_5_out,
       or_6_out, or_7_out, or_8_out, or_9_out, or_10_out, or_11_out, or_12_out, or_13_out, or_14_out,
       or_15_out, or_16_out, or_17_out, or_18_out, or_19_out, or_20_out, or_21_out, or_22_out, or_23_out,
       or_24_out, or_25_out, or_26_out, or_27_out, or_28_out, or_29_out, or_30_out, or_31_out, or_32_out,
       or_33_out, or_34_out, or_35_out;

  not not_1 (not_1_out, w);
  not not_2 (not_2_out, y);
  not not_3 (not_3_out, x);
  not not_4 (not_4_out, z);
  or or_1 (or_1_out, w, x, not_2_out, z);
  or or_2 (or_2_out, w, x, not_2_out, not_4_out);
  or or_3 (or_3_out, w, not_3_out, not_2_out, not_4_out);
  or or_4 (or_4_out, not_1_out, x, y, z);
  or or_5 (or_5_out, not_1_out, x, y, not_4_out);
  or or_6 (or_6_out, not_1_out, x, not_2_out, z);
  or or_7 (or_7_out, not_1_out, x, not_2_out, not_4_out);
  or or_8 (or_8_out, w, x, y, not_4_out);
  or or_9 (or_9_out, w, x, not_2_out, z);
  or or_10 (or_10_out, not_1_out, x, y, not_4_out);
  or or_11 (or_11_out, w, x, y, z);
  or or_12 (or_12_out, w, x, not_2_out, z);
  or or_13 (or_13_out, w, not_3_out, not_2_out, z);
  or or_14 (or_14_out, not_1_out, x, y, not_4_out);
  or or_15 (or_15_out, w, x, not_2_out, z);
  or or_16 (or_16_out, w, x, not_2_out, not_4_out);
  or or_17 (or_17_out, w, not_3_out, not_2_out, not_4_out);
  or or_18 (or_18_out, w, x, y, not_4_out);
  or or_19 (or_19_out, w, x, not_2_out, z);
  or or_20 (or_20_out, w, x, not_2_out, not_4_out);
  or or_21 (or_21_out, w, not_3_out, y, not_4_out);
  or or_22 (or_22_out, w, not_3_out, not_2_out, not_4_out);
  or or_23 (or_23_out, w, x, y, z);
  or or_24 (or_24_out, w, x, not_2_out, z);
  or or_25 (or_25_out, w, x, not_2_out, not_4_out);
  or or_26 (or_26_out, w, not_3_out, y, not_4_out);
  or or_27 (or_27_out, w, not_3_out, not_2_out, z);
  or or_28 (or_28_out, w, not_3_out, not_2_out, not_4_out);
  or or_29 (or_29_out, not_1_out, x, y, z);
  or or_30 (or_30_out, not_1_out, x, not_2_out, z);
  or or_31 (or_31_out, not_1_out, x, not_2_out, not_4_out);
  or or_32 (or_32_out, w, x, not_2_out, not_4_out);
  or or_33 (or_33_out, w, not_3_out, y, z);
  or or_34 (or_34_out, w, not_3_out, not_2_out, not_4_out);
  or or_35 (or_35_out, not_1_out, x, y, not_4_out);
  and and_1 (b, or_8_out, or_9_out, or_10_out);
  and and_2 (c, or_11_out, or_12_out, or_13_out, or_14_out);
  and and_3 (d, or_15_out, or_16_out, or_17_out);
  and and_4 (e, or_18_out, or_19_out, or_20_out, or_21_out, or_22_out);
  and and_5 (g, or_32_out, or_33_out, or_34_out, or_35_out);
  and and_6 (a, or_1_out, or_2_out, or_3_out, or_4_out, or_5_out, or_6_out, or_7_out);
  and and_7 (f, or_23_out, or_24_out, or_25_out, or_26_out, or_27_out, or_28_out, or_29_out, or_30_out, or_31_out);
  _7_Segment_Display u_7_segment_display_1 (.g(g), .f(f), .a(a), .b(b), .e(e), .d(d), .c(c));  // open: dp
endmodule
