// Logisim project SSOP.circ as structural Verilog: 1 circuit, main circuit main
module main (
  input  w,
  input  x,
  input  y,
  input  z,
  output a,
  output b,
  output c,
  output d,
  output e,
  output f,
  output g
);

  wire and_1_out, and_2_out, and_3_out, and_4_out, and_5_out, and_6_out, and_7_out, and_8_out, and_9_out,
       and_10_out, and_11_out, and_12_out, and_13_out, and_14_out, and_15_out, and_16_out, and_17_out,
       and_18_out, and_19_out, and_20_out, and_21_out, and_22_out, and_23_out, and_24_out, and_25_out,
       and_26_out, and_27_out, and_28_out, and_29_out, and_30_out, and_31_out, and_32_out, and_33_out,
       and_34_out, and_35_out, and_36_out, and_37_out, and_38_out, and_39_out, and_40_out, and_41_out,
       and_42_out, and_43_out, and_44_out, and_45_out, and_46_out, and_47_out, and_48_out, and_49_out,
       not_1_out, not_2_out, not_3_out, not_4_out;

  not not_1 (not_1_out, w);
  not not_2 (not_2_out, x);
  not not_3 (not_3_out, y);
  not not_4 (not_4_out, z);
  and and_1 (and_1_out, not_1_out, not_2_out, not_3_out, not_4_out);
  and and_2 (and_2_out, not_1_out, not_2_out, not_3_out, z);
  and and_3 (and_3_out, not_1_out, x, not_3_out, not_4_out);
  and and_4 (and_4_out, not_1_out, x, not_3_out, z);
  and and_5 (and_5_out, not_1_out, x, y, not_4_out);
  and and_6 (and_6_out, not_1_out, not_2_out, not_3_out, not_4_out);
  and and_7 (and_7_out, not_1_out, not_2_out, y, z);
  and and_8 (and_8_out, not_1_out, x, not_3_out, not_4_out);
  and and_9 (and_9_out, not_1_out, x, not_3_out, z);
  and and_10 (and_10_out, not_1_out, x, y, not_4_out);
  and and_11 (and_11_out, not_1_out, x, y, z);
  and and_12 (and_12_out, w, not_2_out, not_3_out, not_4_out);
  and and_13 (and_13_out, w, not_2_out, y, not_4_out);
  and and_14 (and_14_out, w, not_2_out, y, z);
  and and_15 (and_15_out, not_1_out, not_2_out, not_3_out, z);
  and and_16 (and_16_out, not_1_out, not_2_out, y, z);
  and and_17 (and_17_out, not_1_out, x, not_3_out, not_4_out);
  and and_18 (and_18_out, not_1_out, x, not_3_out, z);
  and and_19 (and_19_out, not_1_out, x, y, z);
  and and_20 (and_20_out, w, not_2_out, not_3_out, not_4_out);
  and and_21 (and_21_out, w, not_2_out, y, not_4_out);
  and and_22 (and_22_out, w, not_2_out, y, z);
  and and_23 (and_23_out, not_1_out, not_2_out, not_3_out, not_4_out);
  and and_24 (and_24_out, not_1_out, not_2_out, not_3_out, z);
  and and_25 (and_25_out, not_1_out, x, not_3_out, not_4_out);
  and and_26 (and_26_out, not_1_out, x, not_3_out, z);
  and and_27 (and_27_out, not_1_out, x, y, not_4_out);
  and and_28 (and_28_out, w, not_2_out, not_3_out, not_4_out);
  and and_29 (and_29_out, w, not_2_out, not_3_out, z);
  and and_30 (and_30_out, w, not_2_out, y, not_4_out);
  and and_31 (and_31_out, w, not_2_out, y, z);
  and and_32 (and_32_out, not_1_out, not_2_out, not_3_out, not_4_out);
  and and_33 (and_33_out, not_1_out, x, not_3_out, not_4_out);
  and and_34 (and_34_out, not_1_out, x, y, not_4_out);
  and and_35 (and_35_out, w, not_2_out, not_3_out, not_4_out);
  and and_36 (and_36_out, w, not_2_out, not_3_out, z);
  and and_37 (and_37_out, w, not_2_out, y, not_4_out);
  and and_38 (and_38_out, w, not_2_out, y, z);
  and and_39 (and_39_out, not_1_out, not_2_out, not_3_out, z);
  or or_1 (f, and_39_out, and_40_out, and_41_out);
  and and_40 (and_40_out, not_1_out, x, not_3_out, not_4_out);
  and and_41 (and_41_out, w, not_2_out, not_3_out, z);
  and and_42 (and_42_out, not_1_out, not_2_out, not_3_out, not_4_out);
  and and_43 (and_43_out, not_1_out, not_2_out, not_3_out, z);
  and and_44 (and_44_out, not_1_out, not_2_out, y, not_4_out);
  and and_45 (and_45_out, not_1_out, x, not_3_out, z);
  and and_46 (and_46_out, not_1_out, x, y, not_4_out);
  and and_47 (and_47_out, w, not_2_out, not_3_out, not_4_out);
  and and_48 (and_48_out, w, not_2_out, y, not_4_out);
  and and_49 (and_49_out, w, not_2_out, y, z);
  or or_2 (a, and_1_out, and_2_out, and_3_out, and_4_out, and_5_out);
  or or_3 (b, and_6_out, and_7_out, and_8_out, and_9_out, and_10_out, and_11_out, and_12_out, and_13_out, and_14_out);
  or or_4 (c, and_15_out, and_16_out, and_17_out, and_18_out, and_19_out, and_20_out, and_21_out, and_22_out);
  or or_5 (d, and_23_out, and_24_out, and_25_out, and_26_out, and_27_out, and_28_out, and_29_out, and_30_out, and_31_out);
  or or_6 (e, and_32_out, and_33_out, and_34_out, and_35_out, and_36_out, and_37_out, and_38_out);
  or or_7 (g, and_42_out, and_43_out, and_44_out, and_45_out, and_46_out, and_47_out, and_48_out, and_49_out);
  _7_Segment_Display u_7_segment_display_1 (.g(g), .f(f), .a(a), .b(b), .e(e), .d(d), .c(c));  // open: dp
endmodule
