// Logisim project T.circ as structural Verilog: 1 circuit, main circuit main
module main (
  output A,
  output B,
  output C,
  output D,
  output E,
  output F,
  output G
);

  wire and_1_out, and_2_out, and_3_out, and_4_out, and_5_out, and_6_out, and_7_out, and_8_out, and_9_out,
       and_10_out, and_11_out, and_12_out, and_13_out, and_14_out, and_15_out, and_16_out, and_17_out,
       and_18_out, and_19_out, and_20_out, and_21_out, clock_1_out, FF0_q, FF1_q, FF2_q, FF3_q, FF3_qn,
       not_1_out, not_2_out, not_3_out, not_4_out, or_1_out;

  Clock clock_1 (.out(clock_1_out));
  and and_1 (and_1_out, or_1_out, and_21_out);
  not not_1 (not_1_out, FF3_q);
  T_Flip_Flop FF3 (.T(and_1_out), .clk(clock_1_out), .Q(FF3_q), .Qn(FF3_qn));  // open: reset, preset
  or or_1 (or_1_out, FF3_q, FF2_q);
  not not_2 (not_2_out, FF1_q);
  not not_3 (not_3_out, FF2_q);
  and and_2 (and_2_out, FF3_qn, and_21_out);
  not not_4 (not_4_out, FF0_q);
  and and_3 (and_3_out, not_1_out, not_2_out);
  and and_4 (and_4_out, FF2_q, not_4_out);
  and and_5 (and_5_out, FF3_q, not_4_out);
  and and_6 (and_6_out, FF1_q, FF0_q);
  and and_7 (and_7_out, not_2_out, not_4_out);
  and and_8 (and_8_out, FF3_q, FF1_q);
  and and_9 (and_9_out, FF3_q, not_4_out);
  and and_10 (and_10_out, not_1_out, FF0_q);
  and and_11 (and_11_out, FF2_q, not_2_out);
  and and_12 (and_12_out, FF2_q, not_4_out);
  and and_13 (and_13_out, FF2_q, not_4_out);
  and and_14 (and_14_out, not_2_out, not_4_out);
  and and_15 (and_15_out, FF2_q, not_2_out, not_4_out);
  and and_16 (and_16_out, not_3_out, not_2_out, FF0_q);
  and and_17 (and_17_out, FF3_q, FF1_q);
  and and_18 (and_18_out, not_3_out, not_4_out);
  and and_19 (and_19_out, FF1_q, not_4_out);
  and and_20 (and_20_out, not_1_out, not_2_out, FF0_q);
  T_Flip_Flop FF2 (.T(and_2_out), .clk(clock_1_out), .Q(FF2_q));  // open: Qn, reset, preset
  or or_2 (A, and_3_out, and_4_out);
  or or_3 (B, FF2_q, and_5_out, and_6_out, and_7_out);
  or or_4 (C, and_8_out, and_9_out, and_10_out, and_11_out);
  or or_5 (D, FF3_q, not_2_out, and_12_out);
  or or_6 (E, FF3_q, and_13_out, and_14_out);
  or or_7 (F, and_15_out, and_16_out);
  or or_8 (G, and_17_out, and_18_out, and_19_out, and_20_out);
  T_Flip_Flop FF1 (.T(FF0_q), .clk(clock_1_out), .Q(FF1_q));  // open: Qn, reset, preset
  and and_21 (and_21_out, FF1_q, FF0_q);
  T_Flip_Flop FF0 (.T(1'b1), .clk(clock_1_out), .Q(FF0_q));  // open: Qn, reset, preset
  _7_Segment_Display u_7_segment_display_1 (.g(G), .f(F), .a(A), .b(B), .e(E), .d(D), .c(C));  // open: dp
endmodule
